# Fritzing sketch Wetterstation (saved by Fritzing 0.9.3b)
breadboards: 1

parts:
  Adafruit_HUZZAH_ESP8266_Breakout1 = Adafruit HUZZAH ESP8266 Breakout [part_number=2471]
  U2 = LM2596 step down module
  Bauteil1 = Adafruit CCS811
  Bauteil2 = Adafruit VEML6075 UV Sensor Breakout [part_number=3964]
  C1 = Electrolytic Capacitor [capacitance=0.22mF package="100 mil [THT, electrolytic]"]
  U4 = Voltage Regulator - 3.3V [package="TO220 [THT]"]
  DeepSleep = double row male pin header, 2 pins [form="♂ (male)"]
  Reset = Pushbutton [package="[THT]"]
  R1 = Resistor [tolerance=±5% resistance=2.2k package=THT]
  Flash = double row male pin header, 2 pins [form="♂ (male)"]
  Regensensor = Pushbutton [package=THT]
  R2 = Resistor [tolerance=±5% resistance=1k package=THT]

nets:
  N1: Adafruit_HUZZAH_ESP8266_Breakout1.#13, Bauteil1.!WAKE
  N2: Adafruit_HUZZAH_ESP8266_Breakout1.#12, Bauteil1.!RESET
  N3: Adafruit_HUZZAH_ESP8266_Breakout1.#14, Regensensor.leg0, R2.Pin_0
  N4: Adafruit_HUZZAH_ESP8266_Breakout1.#16, Adafruit_HUZZAH_ESP8266_Breakout1.RST, DeepSleep.pin1, DeepSleep.pin2, R1.Pin_1
  VIN: Adafruit_HUZZAH_ESP8266_Breakout1.EN, Adafruit_HUZZAH_ESP8266_Breakout1.3V, Bauteil1.VIN, Bauteil2.VIN, C1.+, U4.output_voltage, Reset.Pin_1, Reset.Pin_2, R1.Pin_0, Regensensor.leg1
  N5: Adafruit_HUZZAH_ESP8266_Breakout1.#5, Bauteil1.SCL, Bauteil2.SCL
  N6: Adafruit_HUZZAH_ESP8266_Breakout1.#4, Bauteil1.SDA, Bauteil2.SDA
  N7: Adafruit_HUZZAH_ESP8266_Breakout1.#0, Flash.pin2
  GND: Adafruit_HUZZAH_ESP8266_Breakout1.#15, Adafruit_HUZZAH_ESP8266_Breakout1.GND, U2.IN-, U2.OUT-, Bauteil1.GND, Bauteil2.GND, C1.-, U4.GND, Reset.Pin_3, Reset.Pin_4, Flash.pin1, R2.Pin_1
  N8: U2.OUT+, U4.input_voltage

custom parts:
  LM2596 step down module: LM2596 DC-DC step down power supply module 3 A.
  Adafruit VEML6075 UV Sensor Breakout: This little sensor is a great way to add UVA and UVB light sensing to any microcontroller project. The VEML6075 from Vishay has both true UVA and UVB band light sensors and an I2C-controlled ADC that will take readings and integrate them. The sensor also comes with calibration registers so you can easily convert the UVA/UVB readings into the UV Index. Compared to our other UV sensors, this one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
